# Fritzing sketch wiring (saved by Fritzing 0.9.3b)
breadboards: 1

parts:
  Part1 = Arduino Uno (Rev3)  # not connected
  S1 = Toggle Switch [package=THT]  # not connected
  J1 = Basic Servo
  LED1 = smd LED [color="Red (633nm)" package="0805 [SMD]"]
  S2 = Toggle Switch [package=THT]
  BAT1 = BC9VPC [package=bc9vpc]  # not connected
  R1 = Resistor [tolerance=±5% resistance=220 package=THT]
  R2 = Resistor [tolerance=±5% resistance=220 package=THT]
  Part2 = Prototyping Shield

nets:
  N1: J1.gnd, Part2.GND#101
  N2: J1.vcc, Part2.5V#96
  N3: J1.pulse, Part2.D12/MISO
  N4: LED1.cathode, R1.Pin_1, R2.Pin_0
  N5: LED1.anode, Part2.5V#95
  N6: S2.L1, Part2.5V#92
  N7: S2.COM, Part2.D2
  N8: R1.Pin_0, Part2.GND#99
  N9: R2.Pin_1, Part2.GND#100

custom parts:
  Prototyping Shield: The Arduino Uno is a microcontroller board based on the ATmega328 (datasheet). It has 14 digital input/output pins (of which 6 can be used as PWM outputs), 6 analog inputs, a 16 MHz ceramic resonator, a USB connection, a power jack, an ICSP header, and a reset button. It contains everything needed to support the microcontroller; simply connect it to a computer with a USB cable or power it with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
